// Logisim project regfile-insert.circ as structural Verilog: 1 circuit, main circuit main
module main (
  output [7:0] Test,
  output [31:0] ra,
  output [31:0] sp,
  output [31:0] t0,
  output [31:0] t1,
  output [31:0] t2,
  output [31:0] s0,
  output [31:0] s1,
  output [31:0] a0,
  output [31:0] Read_Data_1,
  output [31:0] Read_Data_2,
  output [4:0] rs1,
  output [4:0] rs2,
  output [4:0] rd,
  output RegWEn,
  output [31:0] out_16
);

  wire clk;
  wire [7:0] adder_1_out;

  Clock clock_1 (.out(clk));
  ROM #(.dataWidth(16)) rs1_rs2_rd_RegWEn (.addr(Test), .data({RegWEn, rd, rs2, rs1}));
  Register register_1 (.D(adder_1_out), .clk(clk), .Q(Test));  // open: en, clr
  Adder adder_1 (.a(8'h1), .b(Test), .out(adder_1_out));  // open: cin, cout
  ROM #(.dataWidth(32)) Write_Data (.addr(Test), .data(out_16));
  regfile_main main_1 (
    .rs2(rs2), .rd(rd), .Read_Data_1(Read_Data_1), .Read_Data_2(Read_Data_2), .ra(ra), .sp(sp), .t0(t0),
    .t1(t1), .t2(t2), .s0(s0), .s1(s1), .a0(a0), .rs1(rs1), .Write_Data(out_16), .RegWEn(RegWEn), .clk(clk));

  // Other names for the same wires on the sheet: RF_In[15:0] = {RegWEn, rd, rs2, rs1}; Write_Data[31:0] = out_16

  // Notes on the sheet:
  //   contents of rs1_rs2_rd_RegWEn (hex, n*v repeats v):
  //   8421 8842 8421 8842
  //   contents of Write_Data (hex, n*v repeats v):
  //   ffffbeef dad fffff00d 5678
  //   Your RegFile must fit here!
  //   There should be no red or blue wires, and the result should not be all X's
endmodule
