// Logisim project ex3_test.circ as structural Verilog: 1 circuit, main circuit main
module main (
  output [7:0] out_1,
  output out_2,
  output out_3
);

  wire clock_1_out;
  wire [7:0] adder_1_out;

  Clock clock_1 (.out(clock_1_out));
  Adder adder_1 (.a(8'h1), .b(out_1), .out(adder_1_out));  // open: cin, cout
  Register register_1 (.D(adder_1_out), .clk(clock_1_out), .Q(out_1));  // open: en, clr
  ROM #(.dataWidth(1)) rom_1 (.addr(out_1));  // open: data
  // FSM fsm_1: pin names not known; wires that end beside it: out_3, out_3, out_2

  // Other names for the same wires on the sheet: In1 = out_3; Test[7:0] = out_1

  // Notes on the sheet:
  //   contents of rom_1 (hex, n*v repeats v):
  //   0 1 0 1 1 0 1
  //   Your FSM circuit must fit here!
  //   There should be no red or blue wires, and the result should not be all X's
endmodule
